# Fritzing sketch 74HC595 (saved by Fritzing 1.0.0d)
breadboards: 1

parts:
  U1 = 74HC595 [package="DIP16 [THT]"]
  Part1 = Arduino Nano (Rev3.0)
  R1 = Resistor [tolerance=±5% power=0.25W resistance=220 package=THT]
  LED1 = LED - 5mm [color="Red (633nm)" current=0.030A package="5 mm [THT]"]
  R2 = Resistor [tolerance=±5% power=0.25W resistance=220 package=THT]
  LED2 = LED - 5mm [color="Red (633nm)" current=0.030A package="5 mm [THT]"]
  R3 = Resistor [tolerance=±5% power=0.25W resistance=220 package=THT]
  LED3 = LED - 5mm [color="Red (633nm)" current=0.030A package="5 mm [THT]"]
  R4 = Resistor [tolerance=±5% power=0.25W resistance=220 package=THT]
  LED4 = LED - 5mm [color="Red (633nm)" current=0.030A package="5 mm [THT]"]
  R5 = Resistor [tolerance=±5% power=0.25W resistance=220 package=THT]
  R6 = Resistor [tolerance=±5% power=0.25W resistance=220 package=THT]
  R7 = Resistor [tolerance=±5% power=0.25W resistance=220 package=THT]
  R8 = Resistor [tolerance=±5% power=0.25W resistance=220 package=THT]
  LED5 = LED - 5mm [color="Red (633nm)" current=0.030A package="5 mm [THT]"]
  LED6 = LED - 5mm [color="Red (633nm)" current=0.030A package="5 mm [THT]"]
  LED7 = LED - 5mm [color="Red (633nm)" current=0.030A package="5 mm [THT]"]
  LED8 = LED - 5mm [color="Red (633nm)" current=0.030A package="5 mm [THT]"]

nets:
  N1: U1.Q1, LED2.anode
  N2: U1.Q2, LED3.anode
  N3: U1.Q3, LED4.anode
  N4: U1.Q4, LED8.anode
  N5: U1.Q5, LED6.anode
  N6: U1.Q6, LED5.anode
  N7: U1.Q7, LED7.anode
  GND: U1.GND, U1.OE, Part1.GND, R1.Pin_0, R2.Pin_0, R3.Pin_0, R4.Pin_0, R5.Pin_0, R6.Pin_0, R7.Pin_0, R8.Pin_0
  N8: U1.Q0, LED1.anode
  5V: U1.VCC, Part1.VIN
  N9: R1.Pin_1, LED1.cathode
  N10: R2.Pin_1, LED2.cathode
  N11: R3.Pin_1, LED3.cathode
  N12: R4.Pin_1, LED4.cathode
  N13: R5.Pin_1, LED7.cathode
  N14: R6.Pin_1, LED8.cathode
  N15: R7.Pin_1, LED5.cathode
  N16: R8.Pin_1, LED6.cathode
